# Fritzing sketch Schematic (saved by Fritzing 0.9.5d)

parts:
  LED_1 = LED Sequin - Royal Blue [part_number=1757]
  LED_2 = LED Sequin - Royal Blue [part_number=1757]
  M1 = DOIT Esp32 DevKit v1 (30 pins long, 11 pins width) [part_number=ESP32S-PIN30]

nets:
  N1: LED_1.+, M1.D4
  N2: LED_1.-, LED_2.-, M1.GND
  N3: LED_2.+, M1.D5

custom parts:
  LED Sequin - Royal Blue: Sew a little sparkle into your wearable project with an Adafruit LED Sequin. Simply connect 3 to 6VDC to the + pin and ground to the - pin, and the LED on the board will light up. You can make the LEDs fade and twinkle by using PWM.
  DOIT Esp32 DevKit v1 (30 pins long, 11 pins width): The DOIT Esp32 DevKit v1 is one of the development board created by DOIT to evaluate the ESP-WROOM-32 module. It is based on the ESP32 microcontroller that boasts Wifi, Bluetooth, Ethernet and Low Power support all in a single chip. (vanepp) made breadboard work, adjusted pin numbering and labels and reduced size of schematic and cleaned up pcb. This chip is 30pins long (2 x15) and 11 pins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
